// Logisim project Falcon-X CPU .circ as structural Verilog: 8 circuits, main circuit main
module main (
);

  wire ALU_C, Carry_flag, clock_1_out, Read, REG_WRITE, Write, Zero_flag;
  wire [1:0] DSP_CONTROL, MUX_RESULT;
  wire [2:0] RA, RD, RS;
  wire [3:0] OBCODE;
  wire [5:3] FARF_data;
  wire [7:0] ALU_OUTPUT, DSP_Result, Immediate8, MULT_OUTPUT, OUTPUT_A, OUTPUT_B, program_counter_1_pc,
       RAM_OUTPUT, WriteData;

  Program_Counter program_counter_1 (.Jump_Address(Immediate8), .PC(program_counter_1_pc));
  ROM #(.dataWidth(16)) FARF (.addr(program_counter_1_pc), .data({OBCODE, RA, RS, FARF_data, RD}));
  assign Immediate8 = {{5{1'b0}}, FARF_data};  // Bit_Extender bit_extender_1
  ALU_CONTROL alu_control_1 (
    .Opcode_In(OBCODE), .ALU_Controll(ALU_C), .DSP_Control(DSP_CONTROL), .MemWrite(Write), .MemRead(Read),
    .RegWrite(REG_WRITE), .Result_MUX_Select(MUX_RESULT));
  Clock clock_1 (.out(clock_1_out));
  RAM ram_1 (.addr(Immediate8), .we(Write), .oe(Read), .clk(clock_1_out), .din(OUTPUT_B), .dout(RAM_OUTPUT));
  Register_Specification register_specification_1 (
    .Read_Address_B(RA), .Read_Address_A(RS), .WriteData(WriteData), .WE(REG_WRITE), .WriteAddr(RD),
    .OUTPUT_A(OUTPUT_A), .OUTPUT_B(OUTPUT_B));
  Multiplierr multiplierr_1 (.Input_A(OUTPUT_A), .Input_B(OUTPUT_B), .out_3(MULT_OUTPUT));
  ALU alu_1 (
    .ALU_S(ALU_C), .B(OUTPUT_B), .A(OUTPUT_A), .Carry_flag(Carry_flag), .out_5(ALU_OUTPUT),
    .Zero_flag(Zero_flag));
  DSP dsp_1 (.ALU_DSP(DSP_CONTROL), .Input_A(OUTPUT_A), .MAX_LIMIT(OUTPUT_B), .RESULT_DSP(DSP_Result));
  Multiplexer #(.select(2), .width(8)) multiplexer_1 (
    .in0(ALU_OUTPUT), .in1(DSP_Result), .in2(RAM_OUTPUT), .in3(MULT_OUTPUT), .out(WriteData), .sel(MUX_RESULT));

  // Notes on the sheet:
  //   contents of FARF (hex, n*v repeats v):
  //   1000 1809 6212
endmodule

module Register_Specification (
  input  [2:0] Read_Address_A,
  input  [7:0] WriteData,
  input  WE,
  input  [2:0] WriteAddr,
  input  [2:0] Read_Address_B,
  output [7:0] OUTPUT_A,
  output [7:0] OUTPUT_B
);

  wire button_1_out, clock_1_out, demultiplexer_1_out0, demultiplexer_1_out1, demultiplexer_1_out2,
       demultiplexer_1_out3, demultiplexer_1_out4, demultiplexer_1_out5, demultiplexer_1_out6,
       demultiplexer_1_out7;
  wire [7:0] R0_q, R1_q, R2_q, R3_q, R4_q, R5_q, R6_q, R7_q;

  Demultiplexer #(.select(3)) demultiplexer_1 (
    .out0(demultiplexer_1_out0), .out1(demultiplexer_1_out1), .out2(demultiplexer_1_out2),
    .out3(demultiplexer_1_out3), .out4(demultiplexer_1_out4), .out5(demultiplexer_1_out5),
    .out6(demultiplexer_1_out6), .out7(demultiplexer_1_out7), .in(WE), .sel(WriteAddr));
  Clock clock_1 (.out(clock_1_out));
  Button button_1 (.out(button_1_out));
  Register R0 (.D(WriteData), .en(demultiplexer_1_out0), .clk(clock_1_out), .Q(R0_q), .clr(button_1_out));
  Register R1 (.D(WriteData), .en(demultiplexer_1_out1), .clk(clock_1_out), .Q(R1_q), .clr(button_1_out));
  Register R2 (.D(WriteData), .en(demultiplexer_1_out2), .clk(clock_1_out), .Q(R2_q), .clr(button_1_out));
  Register R3 (.D(WriteData), .en(demultiplexer_1_out3), .clk(clock_1_out), .Q(R3_q), .clr(button_1_out));
  Register R4 (.D(WriteData), .en(demultiplexer_1_out4), .clk(clock_1_out), .Q(R4_q), .clr(button_1_out));
  Register R5 (.D(WriteData), .en(demultiplexer_1_out5), .clk(clock_1_out), .Q(R5_q), .clr(button_1_out));
  Register R6 (.D(WriteData), .en(demultiplexer_1_out6), .clk(clock_1_out), .Q(R6_q), .clr(button_1_out));
  Register R7 (.D(WriteData), .en(demultiplexer_1_out7), .clk(clock_1_out), .Q(R7_q), .clr(button_1_out));
  Multiplexer #(.select(3), .width(8)) multiplexer_1 (
    .in0(R0_q), .in1(R1_q), .in2(R2_q), .in3(R3_q), .in4(R4_q), .in5(R5_q), .in6(R6_q), .in7(R7_q),
    .out(OUTPUT_A), .sel(Read_Address_A));
  Multiplexer #(.select(3), .width(8)) multiplexer_2 (
    .in0(R0_q), .in1(R1_q), .in2(R2_q), .in3(R3_q), .in4(R4_q), .in5(R5_q), .in6(R6_q), .in7(R7_q),
    .out(OUTPUT_B), .sel(Read_Address_B));
endmodule

module Program_Counter (
  input  [7:0] Jump_Address,
  output [7:0] PC
);

  wire button_1_out, clock_1_out;
  wire [7:0] adder_1_out;

  Adder adder_1 (.a(8'h1), .b(PC), .out(adder_1_out));  // open: cin, cout
  Clock clock_1 (.out(clock_1_out));
  Register register_1 (.D(adder_1_out), .en(1'b1), .clk(clock_1_out), .Q(PC), .clr(button_1_out));
  Button button_1 (.out(button_1_out));
endmodule

module ALU (
  input  [7:0] A,
  input  [7:0] B,
  input  ALU_S,
  output Carry_flag,
  output [7:0] out_5,
  output Zero_flag
);

  wire [7:0] adder_1_out, subtractor_1_out;

  Adder adder_1 (.a(A), .b(B), .out(adder_1_out), .cout(Carry_flag));  // open: cin
  Subtractor subtractor_1 (.a(A), .b(B), .out(subtractor_1_out));  // open: bin, bout
  Multiplexer #(.width(8)) multiplexer_1 (.in0(adder_1_out), .in1(subtractor_1_out), .out(out_5), .sel(ALU_S));
  nor nor_1 (Zero_flag, out_5[0], out_5[1], out_5[2], out_5[3], out_5[4], out_5[5], out_5[6], out_5[7]);

  // Other names for the same wires on the sheet: ALU_OUTPUT[7:0] = out_5
endmodule

module Ccomparator (
  input  [7:0] Input_A,
  input  [7:0] Input_B,
  output Greater,
  output Equal,
  output Less
);

  Comparator comparator_1 (.a(Input_A), .b(Input_B), .gt(Greater), .eq(Equal), .lt(Less));
endmodule

module ALU_CONTROL (
  input  [3:0] Opcode_In,
  output MemWrite,
  output MemRead,
  output ALU_Controll,
  output RegWrite,
  output [1:0] DSP_Control,
  output [1:0] Result_MUX_Select
);

  wire ADD, AVG, BEQ, CMP, decoder_1_out14, decoder_1_out15, JMP, MAX, MIN, MUL, NOP, or_6_out, or_7_out,
       or_8_out, or_9_out, SAT, THCMP;

  Decoder #(.enable("false"), .select(4)) decoder_1 (
    .out0(NOP), .out1(MemRead), .out2(MemWrite), .out3(ADD), .out4(ALU_Controll), .out5(MUL), .out6(AVG),
    .out7(MAX), .out8(MIN), .out9(SAT), .out10(THCMP), .out11(CMP), .out12(JMP), .out13(BEQ),
    .out14(decoder_1_out14), .out15(decoder_1_out15), .sel(Opcode_In));
  or or_1 (DSP_Control[0], MAX, SAT);
  or or_2 (DSP_Control[1], MIN, SAT);
  or or_3 (RegWrite, ADD, ALU_Controll, MUL, MemRead, AVG, MAX, MIN, SAT);
  or or_4 (Result_MUX_Select[1], MemRead, MUL);
  or or_5 (Result_MUX_Select[0], AVG, MAX, MIN, SAT, MUL);
  or or_6 (or_6_out, ADD, ALU_Controll);
  or or_7 (or_7_out, AVG, MAX, MIN, SAT);
  or or_8 (or_8_out, JMP, BEQ);
  or or_9 (or_9_out, CMP, THCMP);
  // also tied to GND on the sheet: {decoder_1_out14, decoder_1_out15}

  // Other names for the same wires on the sheet: LOAD = MemRead; STORE = MemWrite; SUB = ALU_Controll
endmodule

module Multiplierr (
  input  [7:0] Input_A,
  input  [7:0] Input_B,
  output [7:0] out_3
);

  Multiplier multiplier_1 (.a(Input_A), .b(Input_B), .out(out_3));  // open: cin, cout
endmodule

module DSP (
  input  [7:0] Input_A,
  input  [1:0] ALU_DSP,
  input  [7:0] MAX_LIMIT,
  output [7:0] RESULT_DSP
);

  wire comparator_1_gt, comparator_1_lt;
  wire [7:0] adder_1_out, AVG, MAX, Min, SAT;

  Adder adder_1 (.a(Input_A), .b(MAX_LIMIT), .out(adder_1_out));  // open: cin, cout
  Comparator comparator_1 (.a(Input_A), .b(MAX_LIMIT), .gt(comparator_1_gt), .lt(comparator_1_lt));  // open: eq
  Shifter #(.shift("lr")) shifter_1 (.in(adder_1_out), .\dist (3'b001), .out(AVG));
  Multiplexer #(.width(8)) multiplexer_1 (.in0(Input_A), .in1(MAX_LIMIT), .out(SAT), .sel(comparator_1_gt));
  Multiplexer #(.width(8)) multiplexer_2 (.in0(Input_A), .in1(MAX_LIMIT), .out(MAX), .sel(comparator_1_lt));
  Multiplexer #(.width(8)) multiplexer_3 (.in0(MAX_LIMIT), .in1(Input_A), .out(Min), .sel(comparator_1_lt));
  Multiplexer #(.select(2), .width(8)) multiplexer_4 (
    .in0(AVG), .in1(MAX), .in2(Min), .in3(SAT), .out(RESULT_DSP), .sel(ALU_DSP));
endmodule
